// Logisim project atto-8.circ as structural Verilog: 1 circuit, main circuit main
module main (
);

  wire and_2_out, and_3_out, and_4_out, and_5_out, and_6_out, and_7_out, and_8_out, button_9_out,
       counter_1_carry, counter_2_carry, demultiplexer_4_out0, demultiplexer_4_out1, demultiplexer_4_out2,
       demultiplexer_4_out3, demultiplexer_4_out4, demultiplexer_4_out5, demultiplexer_4_out6,
       demultiplexer_4_out7, demultiplexer_4_out8, demultiplexer_4_out9, demultiplexer_4_out10,
       demultiplexer_4_out11, demultiplexer_4_out12, demultiplexer_4_out13, demultiplexer_4_out14,
       demultiplexer_4_out15, demultiplexer_4_out16, demultiplexer_4_out17, demultiplexer_4_out18,
       demultiplexer_4_out19, demultiplexer_4_out20, demultiplexer_4_out21, demultiplexer_4_out22,
       demultiplexer_4_out23, demultiplexer_4_out24, demultiplexer_4_out25, demultiplexer_4_out26,
       demultiplexer_4_out27, demultiplexer_4_out28, demultiplexer_4_out29, demultiplexer_4_out30,
       demultiplexer_4_out31, keyboard_1_avail, MC_CLK, MC_DATA_MEM, MC_INHIBIT_MEM, MC_MEM_DATA, MC_RST,
       MC_ZERO, MP_CIN, MP_COUT, MP_COUT_CF, MP_DATA_AL, MP_DATA_IL, MP_DATA_IP, MP_DATA_SP, MP_DATA_XL,
       MP_DATA_YL, MP_DATA_ZL, MP_IP_DATA, MP_NAND_DATA, MP_OFST_DATA, MP_OFST_DATA_FAKE, MP_ONES_DATA,
       MP_SIZE_DATA, MP_SIZE_DATA_FAKE, MP_SP_DATA, MP_SUM_DATA, MP_ZERO, MP_ZERO_CF, MP_ZERO_SC,
       multiplexer_1_out, not_1_out, not_2_out, not_3_out, not_4_out, not_5_out, not_7_out, or_1_out,
       or_2_out, or_3_out, or_5_out, s_r_ff_1_q, s_r_ff_1_qn, undriven;
  wire [3:0] demultiplexer_1_out0, register_7_q;
  wire [4:0] counter_1_q;
  wire [5:5] register_8_q;
  wire [6:0] keyboard_1_data;
  wire [7:0] adder_1_out, button_2_out, MC_ADDR, MC_DATA, MP_ADDR, MP_DATA, multiplexer_2_out, nand_1_out,
       or_4_out, PRELOAD_data, register_1_q, register_2_q, register_3_q, register_5_q, register_6_q,
       register_9_q, register_10_q, register_11_q, register_12_q, register_13_q, register_14_q,
       register_15_q, register_16_q, register_17_q, register_18_q, register_19_q, register_20_q,
       register_21_q, register_22_q, register_23_q, register_24_q, register_25_q, register_26_q,
       register_27_q, register_28_q, register_29_q, register_30_q, register_31_q, register_32_q,
       register_33_q, register_34_q, register_35_q, register_36_q, register_37_q, register_38_q,
       register_39_q, register_40_q;
  wire [7:4] register_7_q_2;
  wire [7:7] not_6_out;
  wire [8:0] counter_2_q;

  nor nor_1 (MC_ZERO, MC_ADDR[0], MC_ADDR[1], MC_ADDR[2], MC_ADDR[3], MC_ADDR[4], MC_ADDR[5], MC_ADDR[6], MC_ADDR[7]);
  S_R_Flip_Flop s_r_ff_1 (
    .S(MC_ZERO), .R(1'b0), .clk(not_1_out), .Q(s_r_ff_1_q), .reset(MC_RST), .Qn(s_r_ff_1_qn), .preset(1'b0));
  // NoConnect on s_r_ff_1_qn
  not not_1 (not_1_out, MC_CLK);
  Register register_1 (.D(MP_DATA), .en(MP_DATA_XL), .clk(MC_CLK), .Q(register_1_q), .clr(MC_RST));
  LedBar ledbar_1 (
    .led0(register_1_q[7]), .led1(register_1_q[6]), .led2(register_1_q[5]), .led3(register_1_q[4]),
    .led4(register_1_q[3]), .led5(register_1_q[2]), .led6(register_1_q[1]), .led7(register_1_q[0]));
  Register register_2 (.D(MP_DATA), .en(MP_DATA_YL), .clk(MC_CLK), .Q(register_2_q), .clr(MC_RST));
  LedBar ledbar_2 (
    .led0(register_2_q[7]), .led1(register_2_q[6]), .led2(register_2_q[5]), .led3(register_2_q[4]),
    .led4(register_2_q[3]), .led5(register_2_q[2]), .led6(register_2_q[1]), .led7(register_2_q[0]));
  Register register_3 (.D(MP_DATA), .en(MP_DATA_ZL), .clk(MC_CLK), .Q(register_3_q), .clr(MC_RST));
  LedBar ledbar_3 (
    .led0(register_3_q[7]), .led1(register_3_q[6]), .led2(register_3_q[5]), .led3(register_3_q[4]),
    .led4(register_3_q[3]), .led5(register_3_q[2]), .led6(register_3_q[1]), .led7(register_3_q[0]));
  Register register_4 (.D(MP_DATA), .en(MP_DATA_AL), .clk(MC_CLK), .Q(MP_ADDR), .clr(MC_RST));
  LedBar ledbar_4 (
    .led0(MP_ADDR[7]), .led1(MP_ADDR[6]), .led2(MP_ADDR[5]), .led3(MP_ADDR[4]), .led4(MP_ADDR[3]),
    .led5(MP_ADDR[2]), .led6(MP_ADDR[1]), .led7(MP_ADDR[0]));
  Register register_5 (.D(MP_DATA), .en(MP_DATA_IP), .clk(MC_CLK), .Q(register_5_q), .clr(MC_RST));
  LedBar ledbar_5 (
    .led0(register_5_q[7]), .led1(register_5_q[6]), .led2(register_5_q[5]), .led3(register_5_q[4]),
    .led4(register_5_q[3]), .led5(register_5_q[2]), .led6(register_5_q[1]), .led7(register_5_q[0]));
  Register register_6 (.D(MP_DATA), .en(MP_DATA_SP), .clk(MC_CLK), .Q(register_6_q), .clr(MC_RST));
  LedBar ledbar_6 (
    .led0(register_6_q[7]), .led1(register_6_q[6]), .led2(register_6_q[5]), .led3(register_6_q[4]),
    .led4(register_6_q[3]), .led5(register_6_q[2]), .led6(register_6_q[1]), .led7(register_6_q[0]));
  and and_1 (MC_INHIBIT_MEM, MC_ZERO, s_r_ff_1_q);
  not not_2 (not_2_out, MC_INHIBIT_MEM);
  RAM #(.asyncread("true"), .databus("bidir")) MEM (
    .addr(MC_ADDR), .we(or_1_out), .oe(and_2_out), .clk(MC_CLK), .data(MC_DATA));
  or or_1 (or_1_out, MC_DATA_MEM, MC_RST);
  and and_2 (and_2_out, MC_MEM_DATA, not_2_out);
  Adder adder_1 (.a(register_1_q), .b(register_2_q), .out(adder_1_out), .cin(MP_CIN), .cout(MP_COUT));
  assign nand_1_out = ~(register_2_q & register_3_q);  // NAND_Gate nand_1, 8 bits wide
  nor nor_2 (MP_ZERO, nand_1_out[0], nand_1_out[1], nand_1_out[2], nand_1_out[3], nand_1_out[4], nand_1_out[5], nand_1_out[6], nand_1_out[7]);
  assign MP_DATA = MP_IP_DATA ? register_5_q : 8'bz;  // Controlled_Buffer controlled_buffer_1
  assign MP_DATA = MP_SP_DATA ? register_6_q : 8'bz;  // Controlled_Buffer controlled_buffer_2
  LedBar ledbar_7 (
    .led0(adder_1_out[7]), .led1(adder_1_out[6]), .led2(adder_1_out[5]), .led3(adder_1_out[4]),
    .led4(adder_1_out[3]), .led5(adder_1_out[2]), .led6(adder_1_out[1]), .led7(adder_1_out[0]));
  LedBar ledbar_8 (
    .led0(nand_1_out[7]), .led1(nand_1_out[6]), .led2(nand_1_out[5]), .led3(nand_1_out[4]),
    .led4(nand_1_out[3]), .led5(nand_1_out[2]), .led6(nand_1_out[1]), .led7(nand_1_out[0]));
  not not_3 (not_3_out, MC_RST);
  assign MC_ADDR = not_3_out ? MP_ADDR : 8'bz;  // Controlled_Buffer controlled_buffer_3
  assign MP_DATA = MP_SUM_DATA ? adder_1_out : 8'bz;  // Controlled_Buffer controlled_buffer_4
  assign MP_DATA = MP_ONES_DATA ? {8{1'b1}} : 8'bz;  // Controlled_Buffer controlled_buffer_5
  assign MP_DATA = MP_NAND_DATA ? nand_1_out : 8'bz;  // Controlled_Buffer controlled_buffer_6
  and and_3 (and_3_out, not_3_out, MC_DATA_MEM);
  assign MC_DATA = and_3_out ? MP_DATA : 8'bz;  // Controlled_Buffer controlled_buffer_7
  LedBar ledbar_9 (
    .led0(MP_DATA[7]), .led1(MP_DATA[6]), .led2(MP_DATA[5]), .led3(MP_DATA[4]), .led4(MP_DATA[3]),
    .led5(MP_DATA[2]), .led6(MP_DATA[1]), .led7(MP_DATA[0]));
  assign MP_DATA = and_4_out ? MC_DATA : 8'bz;  // Controlled_Buffer controlled_buffer_8
  and and_4 (and_4_out, not_3_out, MC_MEM_DATA);
  assign MP_DATA = MP_OFST_DATA ? {4'b0000, register_7_q} : 8'bz;  // Controlled_Buffer controlled_buffer_9
  assign MP_DATA = MP_SIZE_DATA ? {4'b0000, demultiplexer_1_out0} : 8'bz;  // Controlled_Buffer controlled_buffer_10
  or or_2 (or_2_out, MC_RST, MP_ZERO_SC);
  // NoConnect on MC_DATA[7]
  TTY tty_1 (.data(MC_DATA[6:0]), .clk(MC_CLK), .we(and_5_out), .clr(MC_RST));
  Button button_1 (.out(button_2_out[3]));
  and and_5 (and_5_out, MC_ZERO, MC_DATA_MEM);
  Keyboard keyboard_1 (.clk(MC_CLK), .re(and_6_out), .clr(MC_RST), .avail(keyboard_1_avail), .data(keyboard_1_data));
  Demultiplexer #(.select(2)) demultiplexer_1 (
    .out0(demultiplexer_1_out0[0]), .out1(demultiplexer_1_out0[1]), .out2(demultiplexer_1_out0[2]),
    .out3(demultiplexer_1_out0[3]), .in(1'b1), .sel(register_7_q[1:0]));
  LedBar ledbar_10 (
    .led0(register_7_q_2[7]), .led1(register_7_q_2[6]), .led2(register_7_q_2[5]), .led3(register_7_q_2[4]),
    .led4(register_7_q[3]), .led5(register_7_q[2]), .led6(register_7_q[1]), .led7(register_7_q[0]));
  Multiplexer multiplexer_1 (.in0(MP_COUT), .in1(MP_ZERO), .out(multiplexer_1_out), .sel(MP_ZERO_CF));
  or or_3 (or_3_out, MP_ZERO_CF, MP_COUT_CF);
  Counter #(.max('h1f), .width(5)) counter_1 (
    .clr(or_2_out), .load(1'b0), .up(1'b1), .count(not_4_out), .clk(not_5_out), .carry(counter_1_carry),
    .Q(counter_1_q));  // open: D
  not not_4 (not_4_out, MC_RST);
  not not_5 (not_5_out, MC_CLK);
  nor nor_3 (MP_ONES_DATA, MP_SIZE_DATA, MP_OFST_DATA, MP_IP_DATA, MP_SP_DATA, MP_SUM_DATA, MP_NAND_DATA, MC_MEM_DATA);
  Clock #(.highDuration(32), .lowDuration(32)) clock_1 (.out(MC_CLK));
  Button button_2 (.out(button_2_out[0]));
  Button button_3 (.out(button_2_out[7]));
  Button button_4 (.out(button_2_out[2]));
  Button button_5 (.out(button_2_out[1]));
  and and_6 (and_6_out, MC_MEM_DATA, MC_INHIBIT_MEM);
  Register register_7 (.D(MP_DATA), .en(MP_DATA_IL), .clk(MC_CLK), .Q({register_7_q_2, register_7_q}), .clr(MC_RST));
  Register #(.width(1)) register_8 (
    .D(multiplexer_1_out), .en(or_3_out), .clk(MC_CLK), .Q(register_8_q[5]), .clr(MC_RST));
  LedBar #(.matrixcols(1)) ledbar_11 (.led0(register_8_q[5]));
  LedBar #(.matrixcols(5)) ledbar_12 (
    .led0(counter_1_q[4]), .led1(counter_1_q[3]), .led2(counter_1_q[2]), .led3(counter_1_q[1]),
    .led4(counter_1_q[0]));
  Button button_6 (.out(button_2_out[4]));
  Button button_7 (.out(button_2_out[6]));
  Button button_8 (.out(button_2_out[5]));
  not not_6 (not_6_out[7], register_7_q_2[7]);
  assign or_4_out = {{4{not_6_out[7]}}, 4'b0000} | {register_7_q_2, register_7_q};  // OR_Gate or_4, 8 bits wide
  // NoConnect on counter_1_carry
  Button button_9 (.out(button_9_out));
  ROM #(.addrWidth(13), .dataWidth(16)) MIC (
    .addr({or_4_out[6:0], register_8_q[5], counter_1_q}),
    .data({MP_DATA_IL, MP_ZERO_SC, MP_SIZE_DATA_FAKE, MP_OFST_DATA_FAKE, MP_IP_DATA, MP_DATA_IP, MP_SP_DATA, MP_DATA_SP, MP_DATA_AL, MC_MEM_DATA, MC_DATA_MEM, MP_DATA_XL, MP_DATA_YL, MP_DATA_ZL, MP_SUM_DATA, MP_NAND_DATA}));
  // NoConnect on or_4_out[7]
  not not_7 (not_7_out, MC_CLK);
  assign MC_DATA = and_6_out ? multiplexer_2_out : 8'bz;  // Controlled_Buffer controlled_buffer_11
  Multiplexer #(.width(8)) multiplexer_2 (
    .in0(button_2_out), .in1({1'b0, keyboard_1_data}), .out(multiplexer_2_out), .sel(keyboard_1_avail));
  Counter #(.max('h1ff), .width(9)) counter_2 (
    .clr(button_9_out), .load(1'b0), .up(1'b1), .count(MC_RST), .clk(not_7_out), .carry(counter_2_carry),
    .Q(counter_2_q));  // open: D
  Demultiplexer #(.select(2)) demultiplexer_2 (
    .out0(MP_OFST_DATA), .out1(MP_COUT_CF), .out2(MP_ZERO_CF), .in(MP_OFST_DATA_FAKE),
    .sel({MP_NAND_DATA, MP_SUM_DATA}));  // open: out3
  LedBar #(.matrixcols(16)) ledbar_13 (
    .led0(MP_NAND_DATA), .led1(MP_SUM_DATA), .led2(MP_DATA_ZL), .led3(MP_DATA_YL), .led4(MP_DATA_XL),
    .led5(MC_DATA_MEM), .led6(MC_MEM_DATA), .led7(MP_DATA_AL), .led8(MP_DATA_SP), .led9(MP_SP_DATA),
    .led10(MP_DATA_IP), .led11(MP_IP_DATA), .led12(MP_OFST_DATA_FAKE), .led13(MP_SIZE_DATA_FAKE),
    .led14(MP_ZERO_SC), .led15(MP_DATA_IL));
  Demultiplexer demultiplexer_3 (.out0(MP_SIZE_DATA), .out1(MP_CIN), .in(MP_SIZE_DATA_FAKE), .sel(MP_SUM_DATA));
  // NoConnect on counter_2_carry
  not not_8 (MC_RST, counter_2_q[8]);
  assign MC_ADDR = MC_RST ? counter_2_q[7:0] : 8'bz;  // Controlled_Buffer controlled_buffer_12
  ROM PRELOAD (.addr(counter_2_q[7:0]), .data(PRELOAD_data));
  assign MC_DATA = MC_RST ? PRELOAD_data : 8'bz;  // Controlled_Buffer controlled_buffer_13
  Demultiplexer #(.select(5)) demultiplexer_4 (
    .out0(demultiplexer_4_out0), .out1(demultiplexer_4_out1), .out2(demultiplexer_4_out2),
    .out3(demultiplexer_4_out3), .out4(demultiplexer_4_out4), .out5(demultiplexer_4_out5),
    .out6(demultiplexer_4_out6), .out7(demultiplexer_4_out7), .out8(demultiplexer_4_out8),
    .out9(demultiplexer_4_out9), .out10(demultiplexer_4_out10), .out11(demultiplexer_4_out11),
    .out12(demultiplexer_4_out12), .out13(demultiplexer_4_out13), .out14(demultiplexer_4_out14),
    .out15(demultiplexer_4_out15), .out16(demultiplexer_4_out16), .out17(demultiplexer_4_out17),
    .out18(demultiplexer_4_out18), .out19(demultiplexer_4_out19), .out20(demultiplexer_4_out20),
    .out21(demultiplexer_4_out21), .out22(demultiplexer_4_out22), .out23(demultiplexer_4_out23),
    .out24(demultiplexer_4_out24), .out25(demultiplexer_4_out25), .out26(demultiplexer_4_out26),
    .out27(demultiplexer_4_out27), .out28(demultiplexer_4_out28), .out29(demultiplexer_4_out29),
    .out30(demultiplexer_4_out30), .out31(demultiplexer_4_out31), .in(1'b1), .sel(MC_ADDR[4:0]));
  and and_7 (and_7_out, MC_ADDR[5], MC_ADDR[6], MC_ADDR[7]);
  or or_5 (or_5_out, MC_DATA_MEM, MC_RST);
  and and_8 (and_8_out, and_7_out, or_5_out, MC_CLK);
  Register register_9 (.D(MC_DATA), .en(demultiplexer_4_out1), .clk(and_8_out), .Q(register_9_q), .clr(undriven));
  Register register_10 (.D(MC_DATA), .en(demultiplexer_4_out3), .clk(and_8_out), .Q(register_10_q), .clr(undriven));
  Register register_11 (.D(MC_DATA), .en(demultiplexer_4_out5), .clk(and_8_out), .Q(register_11_q), .clr(undriven));
  Register register_12 (.D(MC_DATA), .en(demultiplexer_4_out7), .clk(and_8_out), .Q(register_12_q), .clr(undriven));
  Register register_13 (.D(MC_DATA), .en(demultiplexer_4_out9), .clk(and_8_out), .Q(register_13_q), .clr(undriven));
  Register register_14 (.D(MC_DATA), .en(demultiplexer_4_out11), .clk(and_8_out), .Q(register_14_q), .clr(undriven));
  Register register_15 (.D(MC_DATA), .en(demultiplexer_4_out13), .clk(and_8_out), .Q(register_15_q), .clr(undriven));
  Register register_16 (.D(MC_DATA), .en(demultiplexer_4_out15), .clk(and_8_out), .Q(register_16_q), .clr(undriven));
  Register register_17 (.D(MC_DATA), .en(demultiplexer_4_out14), .clk(and_8_out), .Q(register_17_q), .clr(undriven));
  Register register_18 (.D(MC_DATA), .en(demultiplexer_4_out12), .clk(and_8_out), .Q(register_18_q), .clr(undriven));
  Register register_19 (.D(MC_DATA), .en(demultiplexer_4_out10), .clk(and_8_out), .Q(register_19_q), .clr(undriven));
  Register register_20 (.D(MC_DATA), .en(demultiplexer_4_out8), .clk(and_8_out), .Q(register_20_q), .clr(undriven));
  Register register_21 (.D(MC_DATA), .en(demultiplexer_4_out6), .clk(and_8_out), .Q(register_21_q), .clr(undriven));
  Register register_22 (.D(MC_DATA), .en(demultiplexer_4_out4), .clk(and_8_out), .Q(register_22_q), .clr(undriven));
  Register register_23 (.D(MC_DATA), .en(demultiplexer_4_out2), .clk(and_8_out), .Q(register_23_q), .clr(undriven));
  Register register_24 (.D(MC_DATA), .en(demultiplexer_4_out0), .clk(and_8_out), .Q(register_24_q), .clr(undriven));
  Register register_25 (.D(MC_DATA), .en(demultiplexer_4_out30), .clk(and_8_out), .Q(register_25_q), .clr(undriven));
  Register register_26 (.D(MC_DATA), .en(demultiplexer_4_out28), .clk(and_8_out), .Q(register_26_q), .clr(undriven));
  Register register_27 (.D(MC_DATA), .en(demultiplexer_4_out26), .clk(and_8_out), .Q(register_27_q), .clr(undriven));
  Register register_28 (.D(MC_DATA), .en(demultiplexer_4_out24), .clk(and_8_out), .Q(register_28_q), .clr(undriven));
  Register register_29 (.D(MC_DATA), .en(demultiplexer_4_out22), .clk(and_8_out), .Q(register_29_q), .clr(undriven));
  Register register_30 (.D(MC_DATA), .en(demultiplexer_4_out20), .clk(and_8_out), .Q(register_30_q), .clr(undriven));
  Register register_31 (.D(MC_DATA), .en(demultiplexer_4_out18), .clk(and_8_out), .Q(register_31_q), .clr(undriven));
  Register register_32 (.D(MC_DATA), .en(demultiplexer_4_out16), .clk(and_8_out), .Q(register_32_q), .clr(undriven));
  Register register_33 (.D(MC_DATA), .en(demultiplexer_4_out17), .clk(and_8_out), .Q(register_33_q), .clr(undriven));
  Register register_34 (.D(MC_DATA), .en(demultiplexer_4_out19), .clk(and_8_out), .Q(register_34_q), .clr(undriven));
  Register register_35 (.D(MC_DATA), .en(demultiplexer_4_out21), .clk(and_8_out), .Q(register_35_q), .clr(undriven));
  Register register_36 (.D(MC_DATA), .en(demultiplexer_4_out23), .clk(and_8_out), .Q(register_36_q), .clr(undriven));
  Register register_37 (.D(MC_DATA), .en(demultiplexer_4_out25), .clk(and_8_out), .Q(register_37_q), .clr(undriven));
  Register register_38 (.D(MC_DATA), .en(demultiplexer_4_out27), .clk(and_8_out), .Q(register_38_q), .clr(undriven));
  Register register_39 (.D(MC_DATA), .en(demultiplexer_4_out29), .clk(and_8_out), .Q(register_39_q), .clr(undriven));
  Register register_40 (.D(MC_DATA), .en(demultiplexer_4_out31), .clk(and_8_out), .Q(register_40_q), .clr(undriven));
  DotMatrix #(.inputtype("row"), .matrixcols(8), .matrixrows(8)) dotmatrix_1 (
    .row0(register_24_q), .row1(register_23_q), .row2(register_22_q), .row3(register_21_q),
    .row4(register_20_q), .row5(register_19_q), .row6(register_18_q), .row7(register_17_q));
  DotMatrix #(.inputtype("row"), .matrixcols(8), .matrixrows(8)) dotmatrix_2 (
    .row0(register_32_q), .row1(register_31_q), .row2(register_30_q), .row3(register_29_q),
    .row4(register_28_q), .row5(register_27_q), .row6(register_26_q), .row7(register_25_q));
  // DotMatrix #(.inputtype("row"), .matrixcols(8), .matrixrows(8)) dotmatrix_3: pin names not known; wires that end beside it: register_9_q, register_10_q, register_11_q, register_12_q, register_13_q
  // DotMatrix #(.inputtype("row"), .matrixcols(8), .matrixrows(8)) dotmatrix_4: pin names not known; wires that end beside it: register_14_q, register_15_q, register_16_q, register_33_q, register_34_q, register_35_q, register_36_q, register_37_q, register_38_q, register_39_q, register_40_q

  // Other names for the same wires on the sheet: MP_DATA_MEM = MC_DATA_MEM; MP_MEM_DATA = MC_MEM_DATA;
  //   MP_CLK = MC_CLK; MP_RST = MC_RST

  // Notes on the sheet:
  //   XL
  //   YL
  //   ZL
  //   AL
  //   IP
  //   SP
  //   NAND
  //   MEM
  //   SUM
  //   ADDR
  //   DATA
  //   CLK
  //   IL
  //   SC
  //   . . . . . . . . . . . . . . . . . . . . . . . . . . . . . . . . . . . . . . . . . . . . . . . . . . . . . . . . . . . . . . . . . . . . . . . . . . . . . . . . . . . . . . . . . . . . . . . . . . . . . . . . . . . . . . . . . . . . . . . . . . . . . . . . . . . . . . . . . . . . . . . . . . . . . . . . . . . . . . . . . . . . . . . . 
  //   OFST
  //   SIZE
  //   CF
  //   contents of MIC (hex, n*v repeats v):
  //   890 2402 8044 290 2102 44 2008 82 8 5 9 50 1012 c 2022 9 4000 15*ffff 890 2402 8044 290 2102 44 2008
  //   82 8 5 9 50 3012 c 2022 9 4000 15*ffff 890 2402 8044 290 2102 44 2008 82 8 5 9 50 1012 c 2022 9 4000
  //   15*ffff 890 2402 8044 290 2102 44 2008 82 8 5 9 50 3012 c 2022 9 4000 15*ffff 890 2402 8044 290 2102
  //   44 2008 82 8 5 9 50 1012 c 2022 9 4000 15*ffff 890 2402 8044 290 2102 44 2008 82 8 5 9 50 3012 c
  //   2022 9 4000 15*ffff 890 2402 8044 290 2102 44 2008 82 8 5 9 50 1012 c 2022 9 4000 15*ffff 890 2402
  //   8044 290 2102 44 2008 82 8 5 9 50 3012 c 2022 9 4000 15*ffff 890 2402 8044 290 2102 44 2008 82 8 9
  //   50 3012 c 2022 0 1009 4000 15*ffff 890 2402 8044 290 2102 44 2008 82 8 9 50 1012 c 2022 d 1005 4000
  //   15*ffff 890 2402 8044 290 2102 44 2008 82 8 9 50 3012 c 2022 0 1009 4000 15*ffff 890 2402 8044 290
  //   2102 44 2008 82 8 9 50 1012 c 2022 d 1005 4000 15*ffff 890 2402 8044 290 2102 44 2008 82 8 9 50 3012
  //   c 2022 0 1009 4000 15*ffff 890 2402 8044 290 2102 44 2008 82 8 9 50 1012 c 2022 d 1005 4000 15*ffff
  //   890 2402 8044 290 2102 44 2008 82 8 9 50 3012 c 2022 0 1009 4000 15*ffff 890 2402 8044 290 2102 44
  //   2008 82 8 9 50 1012 c 2022 d 1005 4000 15*ffff 890 2402 8044 fffe 4000 27*ffff 890 2402 8044 fffe
  //   4000 27*ffff 890 2402 8044 fffe 4000 27*ffff 890 2402 8044 fffe 4000 27*ffff 890 2402 8044 fffe 4000
  //   27*ffff 890 2402 8044 fffe 4000 27*ffff 890 2402 8044 fffe 4000 27*ffff 890 2402 8044 fffe 4000
  //   27*ffff 890 2402 8044 fffe 4000 27*ffff 890 2402 8044 fffe 4000 27*ffff 890 2402 8044 fffe 4000
  //   27*ffff 890 2402 8044 fffe 4000 27*ffff 890 2402 8044 fffe 4000 27*ffff 890 2402 8044 fffe 4000
  //   27*ffff 890 2402 8044 fffe 4000 27*ffff 890 2402 8044 fffe 4000 27*ffff 890 2402 8044 290 2102 44
  //   2008 82 50 8 0 0 2022 c 9 4000 16*ffff 890 2402 8044 290 2102 44 2008 82 50 8 5 11 2022 c 9 4000
  //   16*ffff 890 2402 8044 290 2102 44 2008 82 50 8 0 0 2022 c 9 4000 16*ffff 890 2402 8044 290 2102 44
  //   2008 82 50 8 5 11 2022 c 9 4000 16*ffff 890 2402 8044 290 2102 44 2008 82 50 8 0 0 2022 c 9 4000
  //   16*ffff 890 2402 8044 290 2102 44 2008 82 50 8 5 11 2022 c 9 4000 16*ffff 890 2402 8044 290 2102 44
  //   2008 82 50 8 0 0 2022 c 9 4000 16*ffff 890 2402 8044 290 2102 44 2008 82 50 8 5 11 2022 c 9 4000
  //   16*ffff 890 2402 8044 210 2008 82 58 1012 c 9 6 280 50 8 1022 c 9 210 2102 4000 12*ffff 8 5 21 210
  //   2008 82 58 1012 c 9 2006 280 50 8 1022 210 2008 82 0 4000 12*ffff 890 2402 8044 210 2008 82 58 1012
  //   c 9 6 280 50 8 1022 c 9 210 2102 4000 12*ffff 8 5 21 210 2008 82 58 1012 c 9 2006 280 50 8 1022 210
  //   2008 82 0 4000 12*ffff 890 2402 8044 210 2008 82 58 1012 c 9 6 280 50 8 1022 c 9 210 2102 4000
  //   12*ffff 8 5 21 210 2008 82 58 1012 c 9 2006 280 50 8 1022 210 2008 82 0 4000 12*ffff 890 2402 8044
  //   210 2008 82 58 1012 c 9 6 280 50 8 1022 c 9 210 2102 4000 12*ffff 8 5 21 210 2008 82 58 1012 c 9
  //   2006 280 50 8 1022 210 2008 82 0 4000 12*ffff 890 2402 8044 fffe 4000 27*ffff 890 2402 8044 fffe
  //   4000 27*ffff 890 2402 8044 fffe 4000 27*ffff 890 2402 8044 fffe 4000 27*ffff 890 2402 8044 fffe 4000
  //   27*ffff 890 2402 8044 fffe 4000 27*ffff 890 2402 8044 fffe 4000 27*ffff 890 2402 8044 fffe 4000
  //   27*ffff 890 2402 8044 fffe 4000 27*ffff 890 2402 8044 fffe 4000 27*ffff 890 2402 8044 fffe 4000
  //   27*ffff 890 2402 8044 fffe 4000 27*ffff 890 2402 8044 fffe 4000 27*ffff 890 2402 8044 fffe 4000
  //   27*ffff 890 2402 8044 fffe 4000 27*ffff 890 2402 8044 fffe 4000 27*ffff 890 2402 8044 290 2102 44
  //   2008 82 8 11 44 5 200a 1021 c 9 4000 15*ffff 890 2402 8044 290 2102 44 2008 82 8 11 44 5 200a 1021 c
  //   9 4000 15*ffff 890 2402 8044 290 2102 44 2008 82 8 11 44 5 200a 1021 c 9 4000 15*ffff 890 2402 8044
  //   290 2102 44 2008 82 8 11 44 5 200a 1021 c 9 4000 15*ffff 890 2402 8044 290 2102 44 2008 82 8 11 44 5
  //   200a 1021 c 9 4000 15*ffff 890 2402 8044 290 2102 44 2008 82 8 11 44 5 200a 1021 c 9 4000 15*ffff
  //   890 2402 8044 290 2102 44 2008 82 8 11 44 5 200a 1021 c 9 4000 15*ffff 890 2402 8044 290 2102 44
  //   2008 82 8 11 44 5 200a 1021 c 9 4000 15*ffff 890 2402 8044 290 2102 44 2008 82 48 d 1021 c 9 4000
  //   18*ffff 890 2402 8044 290 2102 44 2008 82 48 d 1021 c 9 400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
  //   MIC
  //   RST
  //   Atto-8 Microprocessor
  //   Atto-8 Microcomputer
  //   CTRL
  //   contents of PRELOAD (hex, n*v repeats v):
  //   e8 55 c0 c0 b6 c0 e4 1f b6 a8 ed 1 f 90 e3 f e3
endmodule
