// Logisim project chip.circ as structural Verilog: 1 circuit, main circuit main
module main (
);

  wire A0, A1, A2, A3, A4, A5, A6, A7, A8, A9, A10, A11, A12, and_1_out, and_4_out, and_5_out, button_1_out,
       C_DATA_AL, C_DATA_CF, C_DATA_IL, C_DATA_IP, C_DATA_SP, C_DATA_XL, C_DATA_YL, C_DATA_ZL, CIN, CLK,
       counter_2_carry, COUT, DATA_MEM, DISPLAY, keyboard_1_avail, MEM_DATA, n7400_1_pin3, n7400_1_pin6,
       n7400_1_pin8, n7400_1_pin11, n7400_2_pin3, n7400_2_pin6, n7400_3_pin3, n7400_3_pin6, n7400_3_pin8,
       n7400_3_pin11, n7402_1_pin1, n7402_1_pin4, n7402_1_pin5, n7402_1_pin13, n7402_2_pin1, n7402_2_pin4,
       n7402_2_pin13, n7402_3_pin3, n7432_1_pin3, n7432_1_pin6, n7432_1_pin8, n7432_1_pin11, n7432_2_pin3,
       n7432_2_pin5, n7432_2_pin8, n7432_2_pin9, n7432_2_pin10, n7474_1_pin2, n7474_1_pin9, n7474_2_pin2,
       n7474_2_pin11, n7474_2_pin12, n7474_3_pin2, n74273_1_pin1, n74273_1_pin2, n74273_1_pin5,
       n74273_1_pin6, n74273_1_pin9, n74273_1_pin10, n74273_1_pin12, n74273_1_pin15, n74273_1_pin16,
       n74273_1_pin19, n74273_1_pin20, n74273_2_pin2, n74273_2_pin5, n74273_2_pin6, n74273_2_pin9,
       n74273_2_pin12, n74273_2_pin15, n74273_2_pin16, n74273_2_pin19, n74273_3_pin2, n74273_3_pin5,
       n74273_3_pin6, n74273_3_pin9, n74273_3_pin12, n74273_3_pin15, n74273_3_pin16, n74273_3_pin19,
       n74273_4_pin2, n74273_4_pin5, n74273_4_pin6, n74273_4_pin9, n74273_4_pin12, n74273_4_pin15,
       n74273_4_pin16, n74273_4_pin19, n74273_5_pin2, n74273_5_pin5, n74273_5_pin6, n74273_5_pin9,
       n74273_5_pin12, n74273_5_pin15, n74273_5_pin16, n74273_5_pin19, n74273_6_pin2, n74273_6_pin5,
       n74273_6_pin6, n74273_6_pin9, n74273_6_pin12, n74273_6_pin15, n74273_6_pin16, n74273_6_pin19,
       n74273_7_pin2, n74273_7_pin5, n74273_7_pin6, n74273_7_pin9, n74273_7_pin12, n74273_7_pin15,
       n74273_7_pin16, n74273_7_pin19, n74273_10_pin6, n74273_10_pin9, n74283_1_pin1, n74283_1_pin4,
       n74283_1_pin7, n74283_1_pin10, n74283_1_pin13, n74283_2_pin1, n74283_2_pin4, n74283_2_pin10,
       n74283_2_pin13, N_CLR_SC, N_DATA_AL, N_DATA_CF, N_DATA_IL, N_DATA_IP, N_DATA_MEM, N_DATA_SP,
       N_DATA_XL, N_DATA_YL, N_DATA_ZL, N_IP_DATA, N_MEM_DATA, N_NAND_DATA, N_SET_CIN, N_SP_DATA, N_SUM_DATA,
       N_ZERO, not_1_out, not_2_out, not_3_out, not_4_out, not_5_out, not_6_out, not_7_out, not_8_out,
       not_11_out, not_12_out, or_1_out, or_2_out, RST, s_r_ff_1_q, s_r_ff_1_qn, STDIN, STDOUT;
  wire [1:0] n74273_10_pin5;
  wire [4:0] counter_1_q, undriven;
  wire [6:0] keyboard_1_data;
  wire [7:0] ADDR, button_2_out, DATA, demultiplexer_1_out0, demultiplexer_1_out1, demultiplexer_1_out2,
       demultiplexer_1_out3, demultiplexer_1_out4, demultiplexer_1_out5, demultiplexer_1_out6,
       demultiplexer_1_out7, demultiplexer_1_out8, demultiplexer_1_out9, demultiplexer_1_out10,
       demultiplexer_1_out11, demultiplexer_1_out12, demultiplexer_1_out13, demultiplexer_1_out14,
       demultiplexer_1_out15, demultiplexer_1_out16, demultiplexer_1_out17, demultiplexer_1_out18,
       demultiplexer_1_out19, demultiplexer_1_out20, demultiplexer_1_out21, demultiplexer_1_out22,
       demultiplexer_1_out23, demultiplexer_1_out24, demultiplexer_1_out25, demultiplexer_1_out26,
       demultiplexer_1_out27, demultiplexer_1_out28, demultiplexer_1_out29, demultiplexer_1_out30,
       demultiplexer_1_out31, MEMADDR, MEMDATA, MIC_data, multiplexer_1_out, pull_resistor_1_node, ROM0_data;
  wire [8:0] counter_2_q, undriven_2;
  wire [12:10] not_15_out;
  wire [14:2] undriven_4;
  wire [27:1] undriven_3;

  LedBar #(.matrixcols(10)) ledbar_1 (
    .led0(n74273_1_pin10), .led1(n74273_1_pin10), .led2(n74273_1_pin15), .led3(n74273_1_pin12),
    .led4(n74273_1_pin9), .led5(n74273_1_pin6), .led6(n74273_1_pin19), .led7(n74273_1_pin16),
    .led8(n74273_1_pin5), .led9(n74273_1_pin2));
  LedBar #(.matrixcols(10)) ledbar_2 (
    .led0(n74273_1_pin10), .led1(n74273_1_pin10), .led2(n74273_4_pin9), .led3(n74273_4_pin6),
    .led4(n74273_4_pin5), .led5(n74273_4_pin2), .led6(n74273_4_pin12), .led7(n74273_4_pin15),
    .led8(n74273_4_pin16), .led9(n74273_4_pin19));
  LedBar #(.matrixcols(10)) ledbar_3 (
    .led0(n74273_1_pin10), .led1(n74273_1_pin10), .led2(n74273_3_pin9), .led3(n74273_3_pin6),
    .led4(n74273_3_pin5), .led5(n74273_3_pin2), .led6(n74273_3_pin12), .led7(n74273_3_pin15),
    .led8(n74273_3_pin16), .led9(n74273_3_pin19));
  LedBar #(.matrixcols(10)) ledbar_4 (
    .led0(n74273_1_pin10), .led1(n74273_1_pin10), .led2(n74273_2_pin9), .led3(n74273_2_pin6),
    .led4(n74273_2_pin5), .led5(n74273_2_pin2), .led6(n74273_2_pin12), .led7(n74273_2_pin15),
    .led8(n74273_2_pin16), .led9(n74273_2_pin19));
  _74273 #(.ShowInternalStructure("true"), .VccGndPorts("true")) u_74273_1 (
    .pin1(n74273_1_pin1), .pin2(n74273_1_pin2), .pin3(DATA[0]), .pin4(DATA[1]), .pin5(n74273_1_pin5),
    .pin6(n74273_1_pin6), .pin7(DATA[4]), .pin8(DATA[5]), .pin9(n74273_1_pin9), .pin10(n74273_1_pin10),
    .pin20(n74273_1_pin20), .pin19(n74273_1_pin19), .pin18(DATA[3]), .pin17(DATA[2]), .pin16(n74273_1_pin16),
    .pin15(n74273_1_pin15), .pin14(DATA[7]), .pin13(DATA[6]), .pin12(n74273_1_pin12), .pin11(C_DATA_XL));
  _74273 #(.ShowInternalStructure("true"), .VccGndPorts("true")) u_74273_2 (
    .pin1(n74273_1_pin1), .pin2(n74273_2_pin2), .pin3(DATA[4]), .pin4(DATA[5]), .pin5(n74273_2_pin5),
    .pin6(n74273_2_pin6), .pin7(DATA[6]), .pin8(DATA[7]), .pin9(n74273_2_pin9), .pin10(n74273_1_pin10),
    .pin20(n74273_1_pin20), .pin19(n74273_2_pin19), .pin18(DATA[0]), .pin17(DATA[1]), .pin16(n74273_2_pin16),
    .pin15(n74273_2_pin15), .pin14(DATA[2]), .pin13(DATA[3]), .pin12(n74273_2_pin12), .pin11(C_DATA_IP));
  _74273 #(.ShowInternalStructure("true"), .VccGndPorts("true")) u_74273_3 (
    .pin1(n74273_1_pin1), .pin2(n74273_3_pin2), .pin3(DATA[4]), .pin4(DATA[5]), .pin5(n74273_3_pin5),
    .pin6(n74273_3_pin6), .pin7(DATA[6]), .pin8(DATA[7]), .pin9(n74273_3_pin9), .pin10(n74273_1_pin10),
    .pin20(n74273_1_pin20), .pin19(n74273_3_pin19), .pin18(DATA[0]), .pin17(DATA[1]), .pin16(n74273_3_pin16),
    .pin15(n74273_3_pin15), .pin14(DATA[2]), .pin13(DATA[3]), .pin12(n74273_3_pin12), .pin11(C_DATA_ZL));
  not not_1 (not_1_out, STDIN);
  _74273 #(.ShowInternalStructure("true"), .VccGndPorts("true")) u_74273_4 (
    .pin1(n74273_1_pin1), .pin2(n74273_4_pin2), .pin3(DATA[4]), .pin4(DATA[5]), .pin5(n74273_4_pin5),
    .pin6(n74273_4_pin6), .pin7(DATA[6]), .pin8(DATA[7]), .pin9(n74273_4_pin9), .pin10(n74273_1_pin10),
    .pin20(n74273_1_pin20), .pin19(n74273_4_pin19), .pin18(DATA[0]), .pin17(DATA[1]), .pin16(n74273_4_pin16),
    .pin15(n74273_4_pin15), .pin14(DATA[2]), .pin13(DATA[3]), .pin12(n74273_4_pin12), .pin11(C_DATA_YL));
  and and_1 (and_1_out, MEM_DATA, not_1_out);
  Counter #(.max('h1f), .width(5)) counter_1 (
    .clr(RST), .load(1'b0), .up(1'b1), .count(DISPLAY), .clk(not_2_out), .D(undriven), .Q(counter_1_q));  // open: carry
  not not_2 (not_2_out, CLK);
  // NoConnect on undriven
  _74273 #(.ShowInternalStructure("true"), .VccGndPorts("true")) u_74273_5 (
    .pin1(n74273_1_pin1), .pin2(n74273_5_pin2), .pin3(DATA[0]), .pin4(DATA[1]), .pin5(n74273_5_pin5),
    .pin6(n74273_5_pin6), .pin7(DATA[4]), .pin8(DATA[5]), .pin9(n74273_5_pin9), .pin10(n74273_1_pin10),
    .pin20(n74273_1_pin20), .pin19(n74273_5_pin19), .pin18(DATA[3]), .pin17(DATA[2]), .pin16(n74273_5_pin16),
    .pin15(n74273_5_pin15), .pin14(DATA[7]), .pin13(DATA[6]), .pin12(n74273_5_pin12), .pin11(C_DATA_YL));
  _74273 #(.ShowInternalStructure("true"), .VccGndPorts("true")) u_74273_6 (
    .pin1(n74273_1_pin1), .pin2(n74273_6_pin2), .pin3(DATA[4]), .pin4(DATA[5]), .pin5(n74273_6_pin5),
    .pin6(n74273_6_pin6), .pin7(DATA[6]), .pin8(DATA[7]), .pin9(n74273_6_pin9), .pin10(n74273_1_pin10),
    .pin20(n74273_1_pin20), .pin19(n74273_6_pin19), .pin18(DATA[0]), .pin17(DATA[1]), .pin16(n74273_6_pin16),
    .pin15(n74273_6_pin15), .pin14(DATA[2]), .pin13(DATA[3]), .pin12(n74273_6_pin12), .pin11(C_DATA_YL));
  _74244 #(.ShowInternalStructure("true"), .VccGndPorts("true")) u_74244_1 (
    .pin1(N_IP_DATA), .pin2(n74273_2_pin2), .pin3(DATA[0]), .pin4(n74273_2_pin5), .pin5(DATA[1]),
    .pin6(n74273_2_pin6), .pin7(DATA[2]), .pin8(n74273_2_pin9), .pin9(DATA[3]), .pin10(n74273_1_pin10),
    .pin20(n74273_1_pin20), .pin19(N_IP_DATA), .pin18(DATA[4]), .pin17(n74273_2_pin19), .pin16(DATA[5]),
    .pin15(n74273_2_pin16), .pin14(DATA[6]), .pin13(n74273_2_pin15), .pin12(DATA[7]), .pin11(n74273_2_pin12));
  RAM #(.asyncread("true"), .databus("bidir")) MEM (
    .addr(MEMADDR), .we(or_1_out), .oe(or_2_out), .clk(CLK), .data(MEMDATA));
  or or_1 (or_1_out, DATA_MEM, RST);
  or or_2 (or_2_out, and_1_out, DISPLAY);
  nor nor_1 (STDOUT, ADDR[0], ADDR[1], ADDR[2], ADDR[3], ADDR[4], ADDR[5], ADDR[6], ADDR[7]);
  S_R_Flip_Flop s_r_ff_1 (
    .S(STDOUT), .R(1'b0), .clk(not_3_out), .Q(s_r_ff_1_q), .reset(RST), .Qn(s_r_ff_1_qn), .preset(1'b0));
  not not_3 (not_3_out, MEM_DATA);
  _7432 #(.ShowInternalStructure("true"), .VccGndPorts("true")) u_7432_1 (
    .pin1(DATA[7]), .pin2(DATA[6]), .pin3(n7432_1_pin3), .pin4(DATA[5]), .pin5(DATA[4]), .pin6(n7432_1_pin6),
    .pin7(n74273_1_pin10), .pin14(n74273_1_pin20), .pin13(DATA[3]), .pin12(DATA[2]), .pin11(n7432_1_pin11),
    .pin10(DATA[1]), .pin9(DATA[0]), .pin8(n7432_1_pin8));
  assign MEMADDR = MEM_DATA ? ADDR : 8'bz;  // Controlled_Buffer controlled_buffer_1
  and and_2 (STDIN, STDOUT, s_r_ff_1_q);
  // NoConnect on s_r_ff_1_qn
  assign MEMADDR = DATA_MEM ? ADDR : 8'bz;  // Controlled_Buffer controlled_buffer_2
  assign MEMADDR = DISPLAY ? {3'b111, counter_1_q} : 8'bz;  // Controlled_Buffer controlled_buffer_3
  _74283 #(.ShowInternalStructure("true"), .VccGndPorts("true")) u_74283_1 (
    .pin1(n74283_1_pin1), .pin2(n74273_5_pin9), .pin3(n74273_1_pin9), .pin4(n74283_1_pin4),
    .pin5(n74273_1_pin6), .pin6(n74273_5_pin6), .pin7(n74283_1_pin7), .pin8(n74273_1_pin10),
    .pin16(n74273_1_pin20), .pin15(n74273_5_pin12), .pin14(n74273_1_pin12), .pin13(n74283_1_pin13),
    .pin12(n74273_1_pin15), .pin11(n74273_5_pin15), .pin10(n74283_1_pin10), .pin9(COUT));
  _7432 #(.ShowInternalStructure("true"), .VccGndPorts("true")) u_7432_2 (
    .pin1(n7432_1_pin6), .pin2(n7432_1_pin3), .pin3(n7432_2_pin3), .pin4(n7432_2_pin3), .pin5(n7432_2_pin5),
    .pin6(N_ZERO), .pin7(n74273_1_pin10), .pin14(n74273_1_pin20), .pin13(n7432_1_pin8),
    .pin12(n7432_1_pin11), .pin11(n7432_2_pin5), .pin10(n7432_2_pin10), .pin9(n7432_2_pin9),
    .pin8(n7432_2_pin8));
  _7400 #(.ShowInternalStructure("true"), .VccGndPorts("true")) u_7400_1 (
    .pin1(n74273_3_pin9), .pin2(n74273_6_pin9), .pin3(n7400_1_pin3), .pin4(n74273_3_pin6),
    .pin5(n74273_6_pin6), .pin6(n7400_1_pin6), .pin7(n74273_1_pin10), .pin14(n74273_1_pin20),
    .pin13(n74273_3_pin12), .pin12(n74273_6_pin12), .pin11(n7400_1_pin11), .pin10(n74273_3_pin15),
    .pin9(n74273_6_pin15), .pin8(n7400_1_pin8));
  LedBar #(.matrixcols(10)) ledbar_5 (
    .led0(n74273_1_pin10), .led1(n74273_1_pin10), .led2(n74273_7_pin9), .led3(n74273_7_pin6),
    .led4(n74273_7_pin5), .led5(n74273_7_pin2), .led6(n74273_7_pin12), .led7(n74273_7_pin15),
    .led8(n74273_7_pin16), .led9(n74273_7_pin19));
  assign DATA = MEM_DATA ? MEMDATA : 8'bz;  // Controlled_Buffer controlled_buffer_4
  LED led_1 (.in(N_ZERO));
  _74273 #(.ShowInternalStructure("true"), .VccGndPorts("true")) u_74273_7 (
    .pin1(n74273_1_pin1), .pin2(n74273_7_pin2), .pin3(DATA[4]), .pin4(DATA[5]), .pin5(n74273_7_pin5),
    .pin6(n74273_7_pin6), .pin7(DATA[6]), .pin8(DATA[7]), .pin9(n74273_7_pin9), .pin10(n74273_1_pin10),
    .pin20(n74273_1_pin20), .pin19(n74273_7_pin19), .pin18(DATA[0]), .pin17(DATA[1]), .pin16(n74273_7_pin16),
    .pin15(n74273_7_pin15), .pin14(DATA[2]), .pin13(DATA[3]), .pin12(n74273_7_pin12), .pin11(C_DATA_SP));
  assign MEMDATA = DATA_MEM ? DATA : 8'bz;  // Controlled_Buffer controlled_buffer_5
  _74283 #(.ShowInternalStructure("true"), .VccGndPorts("true")) u_74283_2 (
    .pin1(n74283_2_pin1), .pin2(n74273_5_pin5), .pin3(n74273_1_pin5), .pin4(n74283_2_pin4),
    .pin5(n74273_1_pin2), .pin6(n74273_5_pin2), .pin7(CIN), .pin8(n74273_1_pin10), .pin16(n74273_1_pin20),
    .pin15(n74273_5_pin16), .pin14(n74273_1_pin16), .pin13(n74283_2_pin13), .pin12(n74273_1_pin19),
    .pin11(n74273_5_pin19), .pin10(n74283_2_pin10), .pin9(n74283_1_pin7));
  LED led_2 (.in(COUT));
  _7400 #(.ShowInternalStructure("true"), .VccGndPorts("true")) u_7400_2 (
    .pin1(n7432_2_pin8), .pin2(n7432_2_pin8), .pin3(n7400_2_pin3), .pin4(n7400_2_pin3), .pin5(N_MEM_DATA),
    .pin6(n7400_2_pin6), .pin7(n74273_1_pin10), .pin14(n74273_1_pin20), .pin13(N_IP_DATA), .pin12(N_SP_DATA),
    .pin11(n7432_2_pin9), .pin10(N_SUM_DATA), .pin9(N_NAND_DATA), .pin8(n7432_2_pin10));
  _7400 #(.ShowInternalStructure("true"), .VccGndPorts("true")) u_7400_3 (
    .pin1(n74273_3_pin5), .pin2(n74273_6_pin5), .pin3(n7400_3_pin3), .pin4(n74273_3_pin2),
    .pin5(n74273_6_pin2), .pin6(n7400_3_pin6), .pin7(n74273_1_pin10), .pin14(n74273_1_pin20),
    .pin13(n74273_3_pin16), .pin12(n74273_6_pin16), .pin11(n7400_3_pin11), .pin10(n74273_3_pin19),
    .pin9(n74273_6_pin19), .pin8(n7400_3_pin8));
  Pull_Resistor pull_resistor_1 (.node(pull_resistor_1_node));
  assign pull_resistor_1_node = DISPLAY ? MEMDATA : 8'bz;  // Controlled_Buffer controlled_buffer_6
  Demultiplexer #(.enable("true"), .select(5), .width(8)) demultiplexer_1 (
    .out0(demultiplexer_1_out0), .out1(demultiplexer_1_out1), .out2(demultiplexer_1_out2),
    .out3(demultiplexer_1_out3), .out4(demultiplexer_1_out4), .out5(demultiplexer_1_out5),
    .out6(demultiplexer_1_out6), .out7(demultiplexer_1_out7), .out8(demultiplexer_1_out8),
    .out9(demultiplexer_1_out9), .out10(demultiplexer_1_out10), .out11(demultiplexer_1_out11),
    .out12(demultiplexer_1_out12), .out13(demultiplexer_1_out13), .out14(demultiplexer_1_out14),
    .out15(demultiplexer_1_out15), .out16(demultiplexer_1_out16), .out17(demultiplexer_1_out17),
    .out18(demultiplexer_1_out18), .out19(demultiplexer_1_out19), .out20(demultiplexer_1_out20),
    .out21(demultiplexer_1_out21), .out22(demultiplexer_1_out22), .out23(demultiplexer_1_out23),
    .out24(demultiplexer_1_out24), .out25(demultiplexer_1_out25), .out26(demultiplexer_1_out26),
    .out27(demultiplexer_1_out27), .out28(demultiplexer_1_out28), .out29(demultiplexer_1_out29),
    .out30(demultiplexer_1_out30), .out31(demultiplexer_1_out31), .in(pull_resistor_1_node),
    .sel(counter_1_q), .en(CLK));
  LED led_3 (.in(CIN));
  not not_4 (not_4_out, MEM_DATA);
  not not_5 (not_5_out, DATA_MEM);
  not not_6 (not_6_out, RST);
  _74244 #(.ShowInternalStructure("true"), .VccGndPorts("true")) u_74244_2 (
    .pin1(N_SUM_DATA), .pin2(n74283_2_pin4), .pin3(DATA[3]), .pin4(n74283_2_pin1), .pin5(DATA[2]),
    .pin6(n74283_1_pin4), .pin7(DATA[7]), .pin8(n74283_1_pin1), .pin9(DATA[6]), .pin10(n74273_1_pin10),
    .pin20(n74273_1_pin20), .pin19(N_SUM_DATA), .pin18(DATA[0]), .pin17(n74283_2_pin10), .pin16(DATA[1]),
    .pin15(n74283_2_pin13), .pin14(DATA[4]), .pin13(n74283_1_pin10), .pin12(DATA[5]), .pin11(n74283_1_pin13));
  _74244 #(.ShowInternalStructure("true"), .VccGndPorts("true")) u_74244_3 (
    .pin1(n7400_2_pin6), .pin2(n74273_1_pin20), .pin3(DATA[0]), .pin4(n74273_1_pin20), .pin5(DATA[1]),
    .pin6(n74273_1_pin20), .pin7(DATA[2]), .pin8(n74273_1_pin20), .pin9(DATA[3]), .pin10(n74273_1_pin10),
    .pin20(n74273_1_pin20), .pin19(n7400_2_pin6), .pin18(DATA[4]), .pin17(n74273_1_pin20), .pin16(DATA[5]),
    .pin15(n74273_1_pin20), .pin14(DATA[6]), .pin13(n74273_1_pin20), .pin12(DATA[7]), .pin11(n74273_1_pin20));
  LED led_4 (.in(n7400_2_pin6));
  _74244 #(.ShowInternalStructure("true"), .VccGndPorts("true")) u_74244_4 (
    .pin1(N_NAND_DATA), .pin2(n7400_3_pin6), .pin3(DATA[0]), .pin4(n7400_3_pin3), .pin5(DATA[1]),
    .pin6(n7400_1_pin6), .pin7(DATA[2]), .pin8(n7400_1_pin3), .pin9(DATA[3]), .pin10(n74273_1_pin10),
    .pin20(n74273_1_pin20), .pin19(N_NAND_DATA), .pin18(DATA[4]), .pin17(n7400_3_pin8), .pin16(DATA[5]),
    .pin15(n7400_3_pin11), .pin14(DATA[6]), .pin13(n7400_1_pin8), .pin12(DATA[7]), .pin11(n7400_1_pin11));
  _74244 #(.ShowInternalStructure("true"), .VccGndPorts("true")) u_74244_5 (
    .pin1(N_SP_DATA), .pin2(n74273_7_pin2), .pin3(DATA[0]), .pin4(n74273_7_pin5), .pin5(DATA[1]),
    .pin6(n74273_7_pin6), .pin7(DATA[2]), .pin8(n74273_7_pin9), .pin9(DATA[3]), .pin10(n74273_1_pin10),
    .pin20(n74273_1_pin20), .pin19(N_SP_DATA), .pin18(DATA[4]), .pin17(n74273_7_pin19), .pin16(DATA[5]),
    .pin15(n74273_7_pin16), .pin14(DATA[6]), .pin13(n74273_7_pin15), .pin12(DATA[7]), .pin11(n74273_7_pin12));
  and and_3 (DISPLAY, not_4_out, not_5_out, not_6_out);
  DotMatrix #(.inputtype("row"), .matrixcols(8), .matrixrows(8), .persist(96)) dotmatrix_1 (
    .row0(demultiplexer_1_out0), .row1(demultiplexer_1_out2), .row2(demultiplexer_1_out4),
    .row3(demultiplexer_1_out6), .row4(demultiplexer_1_out8), .row5(demultiplexer_1_out10),
    .row6(demultiplexer_1_out12), .row7(demultiplexer_1_out14));
  DotMatrix #(.inputtype("row"), .matrixcols(8), .matrixrows(8), .persist(96)) dotmatrix_2 (
    .row0(demultiplexer_1_out16), .row1(demultiplexer_1_out18), .row2(demultiplexer_1_out20),
    .row3(demultiplexer_1_out22), .row4(demultiplexer_1_out24), .row5(demultiplexer_1_out26),
    .row6(demultiplexer_1_out28), .row7(demultiplexer_1_out30));
  Clock clock_1 (.out(CLK));
  Button button_1 (.out(button_1_out));
  not not_7 (not_7_out, CLK);
  // DotMatrix #(.inputtype("row"), .matrixcols(8), .matrixrows(8), .persist(96)) dotmatrix_3: pin names not known; wires that end beside it: demultiplexer_1_out1, demultiplexer_1_out3, demultiplexer_1_out5, demultiplexer_1_out7, demultiplexer_1_out9
  // DotMatrix #(.inputtype("row"), .matrixcols(8), .matrixrows(8), .persist(96)) dotmatrix_4: pin names not known; wires that end beside it: demultiplexer_1_out11, demultiplexer_1_out13, demultiplexer_1_out15, demultiplexer_1_out17, demultiplexer_1_out19, demultiplexer_1_out21, demultiplexer_1_out23, demultiplexer_1_out25, demultiplexer_1_out27, demultiplexer_1_out29, demultiplexer_1_out31
  Counter #(.max('h1ff), .width(9)) counter_2 (
    .clr(button_1_out), .load(1'b0), .up(1'b1), .count(RST), .clk(not_7_out), .D(undriven_2),
    .carry(counter_2_carry), .Q(counter_2_q));
  // NoConnect on undriven_2
  not not_8 (not_8_out, CLK);
  not not_9 (n74273_1_pin1, RST);
  // NoConnect on counter_2_carry
  assign MEMADDR = RST ? counter_2_q[7:0] : 8'bz;  // Controlled_Buffer controlled_buffer_7
  ROM ROM0 (.addr(counter_2_q[7:0]), .data(ROM0_data));
  not not_10 (RST, counter_2_q[8]);
  // NoConnect on DATA[7]
  TTY tty_1 (.data(DATA[6:0]), .clk(CLK), .we(and_4_out), .clr(RST));
  and and_4 (and_4_out, STDOUT, DATA_MEM);
  Keyboard #(.buflen(256)) keyboard_1 (
    .clk(CLK), .re(and_5_out), .clr(RST), .avail(keyboard_1_avail), .data(keyboard_1_data));
  and and_5 (and_5_out, MEM_DATA, STDIN);
  not not_11 (not_11_out, CLK);
  not not_12 (not_12_out, RST);
  Button button_2 (.out(button_2_out[0]));
  Button button_3 (.out(button_2_out[2]));
  Button button_4 (.out(button_2_out[3]));
  Button button_5 (.out(button_2_out[1]));
  LedBar #(.matrixcols(10)) ledbar_6 (
    .led0(undriven_3[27]), .led1(undriven_3[27]), .led2(n74283_1_pin10), .led3(n74283_1_pin13),
    .led4(n74283_1_pin1), .led5(n74283_1_pin4), .led6(n74283_2_pin10), .led7(n74283_2_pin13),
    .led8(n74283_2_pin1), .led9(n74283_2_pin4));
  LedBar #(.matrixcols(10)) ledbar_7 (
    .led0(undriven_3[27]), .led1(undriven_3[27]), .led2(n74273_1_pin20), .led3(n74273_1_pin20),
    .led4(n74273_1_pin20), .led5(n74273_1_pin20), .led6(n74273_1_pin20), .led7(n74273_1_pin20),
    .led8(n74273_1_pin20), .led9(n74273_1_pin20));
  LedBar #(.matrixcols(10)) ledbar_8 (
    .led0(undriven_3[27]), .led1(undriven_3[27]), .led2(n7400_1_pin3), .led3(n7400_1_pin6),
    .led4(n7400_3_pin3), .led5(n7400_3_pin6), .led6(n7400_1_pin11), .led7(n7400_1_pin8),
    .led8(n7400_3_pin11), .led9(n7400_3_pin8));
  Button button_6 (.out(button_2_out[4]));
  Button button_7 (.out(button_2_out[6]));
  Button button_8 (.out(button_2_out[7]));
  Button button_9 (.out(button_2_out[5]));
  LedBar #(.matrixcols(10)) ledbar_9 (
    .led0(undriven_3[27]), .led1(undriven_3[27]), .led2(N_DATA_IP), .led3(N_DATA_SP), .led4(N_DATA_CF),
    .led5(N_DATA_IL), .led6(N_DATA_AL), .led7(N_DATA_XL), .led8(N_DATA_YL), .led9(N_DATA_ZL));
  LedBar #(.matrixcols(10)) ledbar_10 (
    .led0(undriven_3[27]), .led1(undriven_3[27]), .led2(DATA[7]), .led3(DATA[6]), .led4(DATA[5]),
    .led5(DATA[4]), .led6(DATA[3]), .led7(DATA[2]), .led8(DATA[1]), .led9(DATA[0]));
  _74273 #(.ShowInternalStructure("true"), .VccGndPorts("true")) u_74273_8 (
    .pin1(not_12_out), .pin2(ADDR[4]), .pin3(DATA[4]), .pin4(DATA[5]), .pin5(ADDR[5]), .pin6(ADDR[6]),
    .pin7(DATA[6]), .pin8(DATA[7]), .pin9(ADDR[7]), .pin10(undriven_3[27]), .pin20(undriven_3[1]),
    .pin19(ADDR[0]), .pin18(DATA[0]), .pin17(DATA[1]), .pin16(ADDR[1]), .pin15(ADDR[2]), .pin14(DATA[2]),
    .pin13(DATA[3]), .pin12(ADDR[3]), .pin11(C_DATA_AL));
  assign MEMDATA = RST ? ROM0_data : 8'bz;  // Controlled_Buffer controlled_buffer_8
  Multiplexer #(.width(8)) multiplexer_1 (
    .in0(button_2_out), .in1({1'b0, keyboard_1_data}), .out(multiplexer_1_out), .sel(keyboard_1_avail));
  assign MEMDATA = and_5_out ? multiplexer_1_out : 8'bz;  // Controlled_Buffer controlled_buffer_9
  _7402 #(.ShowInternalStructure("true"), .VccGndPorts("true")) u_7402_1 (
    .pin1(n7402_1_pin1), .pin2(N_ZERO), .pin3(N_NAND_DATA), .pin4(n7402_1_pin4), .pin5(n7402_1_pin5),
    .pin6(N_SUM_DATA), .pin7(undriven_3[27]), .pin14(undriven_3[1]), .pin13(n7402_1_pin13),
    .pin12(n7402_1_pin1), .pin11(n7402_1_pin4), .pin10(n7402_1_pin5), .pin9(COUT), .pin8(COUT));
  _7474 #(.ShowInternalStructure("true"), .VccGndPorts("true")) u_7474_1 (
    .pin1(N_CLR_SC), .pin2(n7474_1_pin2), .pin3(not_11_out), .pin4(not_12_out), .pin5(A5),
    .pin6(n7474_1_pin2), .pin7(undriven_3[27]), .pin14(undriven_3[1]), .pin13(undriven_3[1]),
    .pin12(n7402_1_pin13), .pin11(C_DATA_CF), .pin10(not_12_out), .pin9(n7474_1_pin9), .pin8(A9));
  LedBar #(.matrixcols(10)) ledbar_11 (
    .led0(undriven_3[27]), .led1(undriven_3[27]), .led2(ADDR[7]), .led3(ADDR[6]), .led4(ADDR[5]),
    .led5(ADDR[4]), .led6(ADDR[3]), .led7(ADDR[2]), .led8(ADDR[1]), .led9(ADDR[0]));
  // NoConnect on n7402_2_pin4
  // NoConnect on n7402_2_pin1
  _7402 #(.ShowInternalStructure("true"), .VccGndPorts("true")) u_7402_2 (
    .pin1(n7402_2_pin1), .pin2(undriven_3[27]), .pin3(undriven_3[27]), .pin4(n7402_2_pin4),
    .pin5(undriven_3[27]), .pin6(undriven_3[27]), .pin7(undriven_3[27]), .pin14(undriven_3[1]),
    .pin13(n7402_2_pin13), .pin12(not_11_out), .pin11(not_11_out), .pin10(CIN), .pin9(N_SET_CIN),
    .pin8(N_SET_CIN));
  // NoConnect on undriven_3[14]
  // NoConnect on n7474_1_pin9
  not not_13 (MEM_DATA, N_MEM_DATA);
  not not_14 (DATA_MEM, N_DATA_MEM);
  _74273 #(.ShowInternalStructure("true"), .VccGndPorts("true")) u_74273_9 (
    .pin1(n7402_2_pin13), .pin2(N_DATA_IL), .pin3(undriven_3[12]), .pin4(undriven_3[11]), .pin5(N_DATA_CF),
    .pin6(N_DATA_SP), .pin7(undriven_3[10]), .pin8(undriven_3[9]), .pin9(N_DATA_IP), .pin10(undriven_3[27]),
    .pin20(undriven_3[1]), .pin19(N_DATA_ZL), .pin18(undriven_3[26]), .pin17(undriven_3[25]),
    .pin16(N_DATA_YL), .pin15(N_DATA_XL), .pin14(undriven_3[24]), .pin13(undriven_3[13]), .pin12(N_DATA_AL),
    .pin11(n7402_2_pin13));
  // NoConnect on undriven_3[2]
  _7474 #(.ShowInternalStructure("true"), .VccGndPorts("true")) u_7474_2 (
    .pin1(N_CLR_SC), .pin2(n7474_2_pin2), .pin3(n7474_1_pin2), .pin4(not_12_out), .pin5(A10),
    .pin6(n7474_2_pin2), .pin7(undriven_3[27]), .pin14(undriven_3[1]), .pin13(N_CLR_SC),
    .pin12(n7474_2_pin12), .pin11(n7474_2_pin11), .pin10(not_12_out), .pin9(A2), .pin8(n7474_2_pin12));
  _7474 #(.ShowInternalStructure("true"), .VccGndPorts("true")) u_7474_3 (
    .pin1(N_CLR_SC), .pin2(n7474_3_pin2), .pin3(n7474_2_pin2), .pin4(not_12_out), .pin5(A1),
    .pin6(n7474_3_pin2), .pin7(undriven_3[27]), .pin14(undriven_3[1]), .pin13(N_CLR_SC),
    .pin12(n7474_2_pin11), .pin11(n7474_3_pin2), .pin10(not_12_out), .pin9(A3), .pin8(n7474_2_pin11));
  _74273 #(.ShowInternalStructure("true"), .VccGndPorts("true")) u_74273_10 (
    .pin1(not_12_out), .pin2(n74273_10_pin5[1]), .pin3(DATA[4]), .pin4(DATA[5]), .pin5(n74273_10_pin5[0]),
    .pin6(n74273_10_pin6), .pin7(DATA[6]), .pin8(DATA[7]), .pin9(n74273_10_pin9), .pin10(undriven_3[27]),
    .pin20(undriven_3[1]), .pin19(A8), .pin18(DATA[0]), .pin17(DATA[1]), .pin16(A0), .pin15(A11),
    .pin14(DATA[2]), .pin13(DATA[3]), .pin12(A12), .pin11(C_DATA_IL));
  _7402 #(.ShowInternalStructure("true"), .VccGndPorts("true")) u_7402_3 (
    .pin1(A7), .pin2(n74273_10_pin5[1]), .pin3(n7402_3_pin3), .pin4(A6), .pin5(n7402_3_pin3),
    .pin6(n74273_10_pin5[0]), .pin7(undriven_3[27]), .pin14(undriven_3[1]), .pin13(A4), .pin12(n7402_3_pin3),
    .pin11(n74273_10_pin6), .pin10(n7402_3_pin3), .pin9(n74273_10_pin9), .pin8(n74273_10_pin9));
  LedBar #(.matrixcols(10)) ledbar_12 (
    .led0(undriven_3[27]), .led1(undriven_3[27]), .led2(undriven_3[9]), .led3(undriven_3[10]),
    .led4(undriven_3[11]), .led5(undriven_3[12]), .led6(undriven_3[13]), .led7(undriven_3[24]),
    .led8(undriven_3[25]), .led9(undriven_3[26]));
  // NoConnect on undriven_4[2]
  // NoConnect on undriven_4[14]
  LedBar #(.matrixcols(10)) ledbar_13 (
    .led0(N_IP_DATA), .led1(N_SP_DATA), .led2(N_MEM_DATA), .led3(N_DATA_MEM), .led4(N_CLR_SC),
    .led5(N_SET_CIN), .led6(N_SUM_DATA), .led7(N_NAND_DATA), .led8(undriven_3[1]), .led9(undriven_3[1]));
  LedBar #(.matrixcols(10)) ledbar_14 (
    .led0(undriven_3[27]), .led1(undriven_3[27]), .led2(A9), .led3(undriven_3[27]), .led4(undriven_3[27]),
    .led5(A2), .led6(A3), .led7(A1), .led8(A10), .led9(A5));
  LedBar #(.matrixcols(10)) ledbar_15 (
    .led0(undriven_3[27]), .led1(undriven_3[27]), .led2(n74273_10_pin9), .led3(n74273_10_pin6),
    .led4(n74273_10_pin5[0]), .led5(n74273_10_pin5[1]), .led6(A12), .led7(A11), .led8(A0), .led9(A8));
  not not_15 (not_15_out[10], A7);
  not not_16 (not_15_out[11], A6);
  not not_17 (not_15_out[12], A4);
  not not_18 (N_IP_DATA, MIC_data[7]);
  not not_19 (N_SP_DATA, MIC_data[6]);
  not not_20 (N_MEM_DATA, MIC_data[5]);
  not not_21 (N_DATA_MEM, MIC_data[4]);
  not not_22 (N_CLR_SC, MIC_data[3]);
  not not_23 (N_SET_CIN, MIC_data[2]);
  not not_24 (N_SUM_DATA, MIC_data[1]);
  not not_25 (N_NAND_DATA, MIC_data[0]);
  ROM #(.addrWidth(13), .dataWidth(16)) MIC (
    .addr({not_15_out, A12, A11, A0, A8, A9, A2, A3, A1, A10, A5}),
    .data({undriven_3[9], undriven_3[10], undriven_3[11], undriven_3[12], undriven_3[13], undriven_3[24], undriven_3[25], undriven_3[26], MIC_data}));
  // also tied to GND on the sheet: {n74273_1_pin10, undriven_3[27]}
  // also tied to VCC on the sheet: {n74273_1_pin20, undriven_3[1]}

  // Other names for the same wires on the sheet: READ = MEM_DATA; WRT = DATA_MEM

  // Notes on the sheet:
  //   XL
  //   YL
  //   ZL
  //   IP
  //   MEM
  //   ZERO
  //   SP
  //   COUT
  //   CIN
  //   PULL
  //   . . . . . . . . . . . . . . . . . . . . . . . . . . . . . . . . . . . . . . . . . . . . . . . . . . . . . . . . . . . . . . . . . . . . . . . . . . . . . . . . . . . . . . . . . . . . . . . . . . . . . . . . . . . . . . . . . . . . . . . . . . . . . . . . . . . . . . . . . . . . . . . . . . . . . . . . . . . . . . . . . . . . . . . . 
  //   CLK
  //   RST
  //   DISPLAY
  //   GND, VCC, DATA7..=DATA0, N_CLK, N_RST
  //   DATA
  //   Atto-8 Microcomputer
  //   SUM
  //   ONES
  //   NAND
  //   ADDR
  //   STDIO
  //   CTRL
  //   DATA
  //   AL
  //   MIC
  //   CTRL
  //   CF
  //   SC
  //   IL
endmodule
